# Fritzing sketch Esquemático (saved by Fritzing 0.9.3b)

parts:
  Esquemático = Raspberry Pi 4B
  Resistor = Resistor [tolerance=±5% resistance=220 package="1206 [SMD]"]
  Relay = RELAY [package=relay-g5q]
  Buzzer = Piezo Speaker
  Squib = Resistor [tolerance=±5% resistance=220 package="1206 [SMD]"]
  Bateria = Battery block 9V
  LED = smd LED [color="Red (633nm)" package="0805 [SMD]"]

nets:
  N1: Esquemático.GND, Resistor.Pin_0, Relay.COIL1, Buzzer.pin1
  N2: Esquemático.GPIO24, LED.anode
  N3: Esquemático.GPIO8, Buzzer.pin2
  N4: Esquemático.GPIO16, Relay.COIL2
  N5: Resistor.Pin_1, LED.cathode
  N6: Relay.MAIN, Bateria.+
  N7: Relay.NO, Squib.Pin_1
  N8: Squib.Pin_0, Bateria.-

// code stored in the sketch: Code.ino
import RPI.GPIO as GPIO
import time

GPIO.setmode(GPIO.BCM) // BCM números depois do GPIO 

led = 24
buzzer = 8
relay = 20

GPIO.setup(led, GPIO.OUT)
GPIO.setup(buzzer, GPIO.OUT)
GPIO.setup(relay, GPIO.OUT)


button_press = True // Estado do botão 

if button_press:
    for contagem_regre in range(10, 0, -1):
       print(contagem_regre)
       GPIO.output(buzzer, GPIO.HIGH)
       print("Beep")
       time.sleep(1)
       
       // Opção para cancelar a ignição
       if(button_press == False):
           print("Bot?o cancelar pressionado, rel? desligado.")
           GPIO.output(relay, GPIO.LOW)
           break
    
    GPIO.output(buzzer, GPIO.LOW)
    GPIO.output(led, GPIO.HIGH)
    GPIO.output(relay, GPIO.HIGH)
    print("\nRel? e led acionados.")

GPIO.cleanup() //Limpar/desconfigurar todos os pinos GPIO
